# Fritzing sketch wiring (saved by Fritzing 0.9.10b)

parts:
  Raspberry_Pi2 = Raspberry Pi B+
  RHT1 = Humidity and Temperature Sensor RHT03
  Bauteil1 = BME280 Breakout  # not connected
  Part1 = SCD30  # not connected
  SDS1 = SDS011 - dust sensor [part_number=1]  # not connected
  Bauteil2 = VEML6070 [part_number=VEML6070]  # not connected
  Bauteil3 = Adafruit MiCS-5524 Gas Sensor [part_number="Adafruit #3199"]  # not connected

nets:
  N1: Raspberry_Pi2.GND, RHT1.GND_1
  5V: Raspberry_Pi2.5V, RHT1.Vcc

custom parts:
  SCD30: CO2 , humidity, and temperature sensor * Current consumption: 19 mA @ 1 meas. per 2 s. * Digital interface UART or I2C * Company: Sensirion - The Sensor Company Electrical specifications * average current: 19 mA * max. current: 75 mA * DC supply: 3.3 V - 5.5 V Operation conditions * temperature: 0 – 50°C * humidity: 0 – 95 %RH * sensor lifetime: 15 years CO2-sensor: * NDIR CO 2 sensor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
  SDS011 - dust sensor: The SDS 011 Sensor is a quite recent Air Quality Sensor developed by inovafit, a spin-off from the university of Jinan (in Shandong). With its size, it is probably one of the best sensor in terms of accuracy: While other sensors tend to focus on shrinking the sensor size, the SDS 011 has opted for a size tradeoff allowing it to use a larger fan. And the larger the fan, the better the quality.
  VEML6070: This little sensor is a great way to add UV light sensing to any microcontroller project. The VEML6070 from Vishay has a true UV A light sensor and an I2C-controlled ADC that will take readings and integrate them for you over ~60ms to 500ms.
  Adafruit MiCS-5524 Gas Sensor: Give your next sensor project a nose for gasses with the Adafruit MiCS-5524 Gas Sensor Breakout. This breakout makes it easy to use this nice sensor from SGX Sensortech. The MiCS-5524 is a robust MEMS sensor for indoor carbon monoxide and natural gas leakage detection, it's suitable also for indoor air quality monitoring; breath checker and early fire detection. Please note: This sensor is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
